# Fritzing sketch fritzing (saved by Fritzing 0.9.3b)
breadboards: 1

parts:
  Raspberry_Pi_1 = Raspberry Pi 3 [part_number=RPI-3-V1.2]
  R2 = Resistor [tolerance=±5% resistance=330 package=THT]
  R3 = Resistor [tolerance=±5% resistance=330 package=THT]
  LED1 = LED - 5mm [color="Green (555nm)" package="5 mm [THT]"]
  LED2 = LED - 5mm [color="Yellow (595nm)" package="5 mm [THT]"]

nets:
  N1: Raspberry_Pi_1.GIPO17, LED2.anode
  N2: Raspberry_Pi_1.GIPO18, LED1.anode
  N3: Raspberry_Pi_1.GND, R2.Pin_0, R3.Pin_0
  N4: R2.Pin_1, LED1.cathode
  N5: R3.Pin_1, LED2.cathode
